# Fritzing sketch Motion activated rgb adressable strip (saved by Fritzing 0.9.10b)
circuit board: 16.805cm x 9.8804cm

parts:
  PIR1 = PIR sensor
  PIR2 = PIR sensor
  YwRobot_Power_Supply1 = YwRobot Breadboard Power Supply [part_number=545043]
  U1 = WS2812 RGB LED strip
  Mod1 = Amica NodeMCU DEVKIT 1.0
  U2 = WS2812 RGB LED strip
  BAT1 = BC9VPC [package=bc9vpc]
  USBTTL1 = Micro USB B Plug
  USBTTL2 = USB A Plug

nets:
  VDD: PIR1.VDD, PIR2.VDD, Mod1.pin1, Mod1.pin_10, Mod1.pin_26
  N1: PIR1.SIG, PIR2.SIG, Mod1.pin_14
  GND: PIR1.GND, PIR2.GND, YwRobot_Power_Supply1.GND#11, U1.GND#0, Mod1.pin2, Mod1.pin_9, Mod1.pin_25
  N2: YwRobot_Power_Supply1.VCC#5, U1.VCC#1
  N3: YwRobot_Power_Supply1.VCC#10, BAT1.V+
  N4: YwRobot_Power_Supply1.GND#14, BAT1.V-
  N5: U1.DIN, Mod1.pin_13
  N6: U1.GND#4, U2.GND
  N7: U1.VCC#5, U2.VCC
  N8: U1.DOUT, U2.DIN
  N9: USBTTL1.usb, USBTTL2.usb

custom parts:
  YwRobot Breadboard Power Supply: The YwRobot Breadboard Power Supply (MB-V2) has two power rails; they can be 5V or 3V3. Power to the module can be provided through the female USB socket or through the A10 (female) 2.1mm power jack.
  WS2812 RGB LED strip: WS2812 strip
